# Fritzing sketch drawings motor hack (saved by Fritzing 0.9.3b)
perfboards: 2

parts:
  M1 = DC Motor
  S1 = Round Pushbutton
  M2 = DC Motor
  Power_plug1 = Power plug
  U1 = Voltage Regulator - 5V [package="TO220 [THT]"]  # not connected
  U2 = Voltage Regulator - 5V [package="TO220 [THT]"]  # not connected
  Power_plug2 = Power plug
  J1 = female pin header, 1 pin [form="♀ (female)"]

nets:
  N1: M1.pin_2, S1.leg0
  N2: S1.leg1, Power_plug2.GND, J1.pin1
  N3: M2.pin_2, Power_plug1.GND
